// Logisim project ALU_Control.circ as structural Verilog: 1 circuit, main circuit ALU_Control
module ALU_Control (
  input  [1:0] ALU_op,
  input  [2:0] Funct3,
  input  Funct7,
  input  op,
  output [2:0] ALU_Control
);

  wire and_1_out, comparator_1_eq, comparator_2_eq, comparator_3_eq, comparator_4_eq, comparator_5_eq,
       comparator_6_eq, comparator_7_eq, comparator_8_eq, or_3_out;
  wire [2:0] multiplexer_1_out, multiplexer_2_out, multiplexer_3_out, multiplexer_4_out, multiplexer_5_out,
       multiplexer_6_out, multiplexer_7_out, or_1_out, or_2_out;

  Comparator #(.width(3)) comparator_1 (.a(Funct3), .b(3'b000), .eq(comparator_1_eq));  // open: gt, lt
  Comparator #(.width(2)) comparator_2 (.a({op, Funct7}), .b(2'b11), .eq(comparator_2_eq));  // open: gt, lt
  Comparator #(.width(3)) comparator_3 (.a(Funct3), .b(3'b010), .eq(comparator_3_eq));  // open: gt, lt
  Comparator #(.width(3)) comparator_4 (.a(Funct3), .b(3'b110), .eq(comparator_4_eq));  // open: gt, lt
  Comparator #(.width(3)) comparator_5 (.a(Funct3), .b(3'b111), .eq(comparator_5_eq));  // open: gt, lt
  Comparator #(.width(2)) comparator_6 (.a(ALU_op), .b(2'b00), .eq(comparator_6_eq));  // open: gt, lt
  Comparator #(.width(2)) comparator_7 (.a(ALU_op), .b(2'b01), .eq(comparator_7_eq));  // open: gt, lt
  Comparator #(.width(2)) comparator_8 (.a(ALU_op), .b(2'b10), .eq(comparator_8_eq));  // open: gt, lt
  Multiplexer #(.width(3), .enable("false")) multiplexer_1 (
    .in0(3'b000), .in1(3'b010), .out(multiplexer_1_out), .sel(comparator_3_eq));
  Multiplexer #(.width(3), .enable("false")) multiplexer_2 (
    .in0(3'b000), .in1(3'b011), .out(multiplexer_2_out), .sel(comparator_4_eq));
  Multiplexer #(.width(3), .enable("false")) multiplexer_3 (
    .in0(3'b000), .in1(3'b100), .out(multiplexer_3_out), .sel(comparator_5_eq));
  Multiplexer #(.width(3), .enable("false")) multiplexer_4 (
    .in0(3'b000), .in1(3'b000), .out(multiplexer_4_out), .sel(comparator_6_eq));
  Multiplexer #(.width(3), .enable("false")) multiplexer_5 (
    .in0(3'b000), .in1(3'b001), .out(multiplexer_5_out), .sel(comparator_7_eq));
  Multiplexer #(.width(3), .enable("false")) multiplexer_6 (
    .in0(3'b000), .in1(or_2_out), .out(multiplexer_6_out), .sel(comparator_8_eq));
  Multiplexer #(.width(3), .enable("false")) multiplexer_7 (
    .in0(3'b000), .in1(3'b001), .out(multiplexer_7_out), .sel(and_1_out));
  and and_1 (and_1_out, comparator_1_eq, comparator_2_eq);
  assign or_1_out = multiplexer_4_out | multiplexer_5_out | multiplexer_6_out;  // OR_Gate or_1, 3 bits wide
  assign or_2_out = multiplexer_7_out | multiplexer_1_out | multiplexer_2_out | multiplexer_3_out;  // OR_Gate or_2, 3 bits wide
  Multiplexer #(.select(3), .width(3)) multiplexer_8 (
    .in0(3'b000), .in1(3'b001), .in2(3'b101), .in3(3'b011), .in4(3'b010), .in5(3'b000), .in6(3'b000),
    .in7(3'b000), .out(ALU_Control), .sel(or_1_out), .en(or_3_out));
  or or_3 (or_3_out, comparator_6_eq, comparator_7_eq, comparator_8_eq);
endmodule
