// Logisim project Control_unit.circ as structural Verilog: 1 circuit, main circuit Control_Unit
module Control_Unit (
  input  [6:0] Opcode,
  output [8:0] Controls
);

  wire comparator_1_eq, comparator_2_eq, comparator_3_eq, comparator_4_eq, or_2_out;
  wire [2:0] multiplexer_1_out, multiplexer_2_out, multiplexer_3_out, multiplexer_4_out, or_1_out;

  Comparator #(.width(7)) comparator_1 (.a(Opcode), .b(7'b0000011), .eq(comparator_1_eq));  // open: gt, lt
  Comparator #(.width(7)) comparator_2 (.a(Opcode), .b(7'b0100011), .eq(comparator_2_eq));  // open: gt, lt
  Comparator #(.width(7)) comparator_3 (.a(Opcode), .b(7'b0110011), .eq(comparator_3_eq));  // open: gt, lt
  Comparator #(.width(7)) comparator_4 (.a(Opcode), .b(7'b1100011), .eq(comparator_4_eq));  // open: gt, lt
  Multiplexer #(.width(3)) multiplexer_1 (
    .in0(3'b000), .in1(3'b000), .out(multiplexer_1_out), .sel(comparator_1_eq), .en(1'b1));
  Multiplexer #(.width(3)) multiplexer_2 (
    .in0(3'b000), .in1(3'b001), .out(multiplexer_2_out), .sel(comparator_2_eq), .en(1'b1));
  Multiplexer #(.width(3)) multiplexer_3 (
    .in0(3'b000), .in1(3'b010), .out(multiplexer_3_out), .sel(comparator_3_eq), .en(1'b1));
  Multiplexer #(.width(3)) multiplexer_4 (
    .in0(3'b000), .in1(3'b011), .out(multiplexer_4_out), .sel(comparator_4_eq), .en(1'b1));
  assign or_1_out = multiplexer_1_out | multiplexer_2_out | multiplexer_3_out | multiplexer_4_out;  // OR_Gate or_1, 3 bits wide
  Multiplexer #(.select(3), .width(9)) multiplexer_5 (
    .in0(9'h128), .in1(9'h70), .in2(9'h102), .in3(9'h85), .in4({9{1'b0}}), .in5({9{1'b0}}), .in6({9{1'b0}}),
    .in7({9{1'b0}}), .out(Controls), .sel(or_1_out), .en(or_2_out));
  or or_2 (or_2_out, comparator_1_eq, comparator_2_eq, comparator_3_eq, comparator_4_eq);
endmodule
