// Logisim project Extender.circ as structural Verilog: 1 circuit, main circuit Extender
module Extender (
  input  [24:0] Data_in,
  input  [1:0] Imm_Src,
  output [31:0] Extender_out
);

  wire [11:0] multiplexer_1_out;

  Multiplexer #(.select(2), .width(12)) multiplexer_1 (
    .in0(Data_in[24:13]), .in1({Data_in[24:18], Data_in[4:0]}),
    .in2({Data_in[24], Data_in[0], Data_in[23:18], Data_in[4:1]}), .in3({12{1'b0}}), .out(multiplexer_1_out),
    .sel(Imm_Src), .en(1'b1));
  assign Extender_out = {{20{multiplexer_1_out[11]}}, multiplexer_1_out};  // Bit_Extender bit_extender_1
endmodule
