// Logisim project Register_file.circ as structural Verilog: 1 circuit, main circuit Register_File
module Register_File (
  input  Clk,
  input  [4:0] A1,
  input  [31:0] WD3,
  input  [4:0] A3,
  input  WE,
  input  [4:0] A2,
  output [31:0] RD1,
  output [31:0] RD2
);

  wire and_1_out, comparator_1_eq, comparator_2_eq, comparator_3_eq, not_1_out, not_2_out, not_3_out;
  wire [31:0] demultiplexer_1_out1, demultiplexer_1_out2, demultiplexer_1_out3, demultiplexer_1_out4,
       demultiplexer_1_out5, demultiplexer_1_out6, demultiplexer_1_out7, demultiplexer_1_out8,
       demultiplexer_1_out9, demultiplexer_1_out10, demultiplexer_1_out11, demultiplexer_1_out12,
       demultiplexer_1_out13, demultiplexer_1_out14, demultiplexer_1_out15, demultiplexer_1_out16,
       demultiplexer_1_out17, demultiplexer_1_out18, demultiplexer_1_out19, demultiplexer_1_out20,
       demultiplexer_1_out21, demultiplexer_1_out22, demultiplexer_1_out23, demultiplexer_1_out24,
       demultiplexer_1_out25, demultiplexer_1_out26, demultiplexer_1_out27, demultiplexer_1_out28,
       demultiplexer_1_out29, demultiplexer_1_out30, demultiplexer_1_out31, Reg_1__2_2, Reg_1__3_2,
       Reg_1__4_2, Reg_1__5_2, Reg_1__6_2, Reg_1__7_2, Reg_1__8_2, Reg_2__1_2, Reg_2__2_2, Reg_2__3_2,
       Reg_2__4_2, Reg_2__5_2, Reg_2__6_2, Reg_2__7_2, Reg_2__8_2, Reg_3__1_2, Reg_3__2_2, Reg_3__3_2,
       Reg_3__4_2, Reg_3__5_2, Reg_3__6_2, Reg_3__7_2, Reg_3__8_2, Reg_4__1_2, Reg_4__2_2, Reg_4__3_2,
       Reg_4__4_2, Reg_4__5_2, Reg_4__6_2, Reg_4__7_2, Reg_4__8_2;

  Comparator #(.width(5)) comparator_1 (.a(A3), .b({5{1'b0}}), .eq(comparator_1_eq));  // open: gt, lt
  not not_1 (not_1_out, comparator_1_eq);
  Demultiplexer #(.select(5), .width(32)) demultiplexer_1 (
    .out1(demultiplexer_1_out1), .out2(demultiplexer_1_out2), .out3(demultiplexer_1_out3),
    .out4(demultiplexer_1_out4), .out5(demultiplexer_1_out5), .out6(demultiplexer_1_out6),
    .out7(demultiplexer_1_out7), .out8(demultiplexer_1_out8), .out9(demultiplexer_1_out9),
    .out10(demultiplexer_1_out10), .out11(demultiplexer_1_out11), .out12(demultiplexer_1_out12),
    .out13(demultiplexer_1_out13), .out14(demultiplexer_1_out14), .out15(demultiplexer_1_out15),
    .out16(demultiplexer_1_out16), .out17(demultiplexer_1_out17), .out18(demultiplexer_1_out18),
    .out19(demultiplexer_1_out19), .out20(demultiplexer_1_out20), .out21(demultiplexer_1_out21),
    .out22(demultiplexer_1_out22), .out23(demultiplexer_1_out23), .out24(demultiplexer_1_out24),
    .out25(demultiplexer_1_out25), .out26(demultiplexer_1_out26), .out27(demultiplexer_1_out27),
    .out28(demultiplexer_1_out28), .out29(demultiplexer_1_out29), .out30(demultiplexer_1_out30),
    .out31(demultiplexer_1_out31), .in(WD3), .sel(A3), .en(and_1_out));  // open: out0
  and and_1 (and_1_out, not_1_out, WE);
  internal_registers_main Reg_1 (
    .clk(Clk), ._1({32{1'b0}}), ._2(demultiplexer_1_out1), ._3(demultiplexer_1_out2),
    ._4(demultiplexer_1_out3), ._5(demultiplexer_1_out4), ._6(demultiplexer_1_out5),
    ._7(demultiplexer_1_out6), ._8(demultiplexer_1_out7), .Enable(and_1_out), ._2_2(Reg_1__2_2),
    ._3_2(Reg_1__3_2), ._4_2(Reg_1__4_2), ._5_2(Reg_1__5_2), ._6_2(Reg_1__6_2), ._7_2(Reg_1__7_2),
    ._8_2(Reg_1__8_2));  // open: _1_2
  internal_registers_main Reg_2 (
    .clk(Clk), ._1(demultiplexer_1_out8), ._2(demultiplexer_1_out9), ._3(demultiplexer_1_out10),
    ._4(demultiplexer_1_out11), ._5(demultiplexer_1_out12), ._6(demultiplexer_1_out13),
    ._7(demultiplexer_1_out14), ._8(demultiplexer_1_out15), .Enable(and_1_out), ._1_2(Reg_2__1_2),
    ._2_2(Reg_2__2_2), ._3_2(Reg_2__3_2), ._4_2(Reg_2__4_2), ._5_2(Reg_2__5_2), ._6_2(Reg_2__6_2),
    ._7_2(Reg_2__7_2), ._8_2(Reg_2__8_2));
  internal_registers_main Reg_3 (
    .clk(Clk), ._1(demultiplexer_1_out16), ._2(demultiplexer_1_out17), ._3(demultiplexer_1_out18),
    ._4(demultiplexer_1_out19), ._5(demultiplexer_1_out20), ._6(demultiplexer_1_out21),
    ._7(demultiplexer_1_out22), ._8(demultiplexer_1_out23), .Enable(and_1_out), ._1_2(Reg_3__1_2),
    ._2_2(Reg_3__2_2), ._3_2(Reg_3__3_2), ._4_2(Reg_3__4_2), ._5_2(Reg_3__5_2), ._6_2(Reg_3__6_2),
    ._7_2(Reg_3__7_2), ._8_2(Reg_3__8_2));
  internal_registers_main Reg_4 (
    .clk(Clk), ._1(demultiplexer_1_out24), ._2(demultiplexer_1_out25), ._3(demultiplexer_1_out26),
    ._4(demultiplexer_1_out27), ._5(demultiplexer_1_out28), ._6(demultiplexer_1_out29),
    ._7(demultiplexer_1_out30), ._8(demultiplexer_1_out31), .Enable(and_1_out), ._1_2(Reg_4__1_2),
    ._2_2(Reg_4__2_2), ._3_2(Reg_4__3_2), ._4_2(Reg_4__4_2), ._5_2(Reg_4__5_2), ._6_2(Reg_4__6_2),
    ._7_2(Reg_4__7_2), ._8_2(Reg_4__8_2));
  Multiplexer #(.select(5), .width(32)) multiplexer_1 (
    .in0({32{1'b0}}), .in1(Reg_1__2_2), .in2(Reg_1__3_2), .in3(Reg_1__4_2), .in4(Reg_1__5_2),
    .in5(Reg_1__6_2), .in6(Reg_1__7_2), .in7(Reg_1__8_2), .in8(Reg_2__1_2), .in9(Reg_2__2_2),
    .in10(Reg_2__3_2), .in11(Reg_2__4_2), .in12(Reg_2__5_2), .in13(Reg_2__6_2), .in14(Reg_2__7_2),
    .in15(Reg_2__8_2), .in16(Reg_3__1_2), .in17(Reg_3__2_2), .in18(Reg_3__3_2), .in19(Reg_3__4_2),
    .in20(Reg_3__5_2), .in21(Reg_3__6_2), .in22(Reg_3__7_2), .in23(Reg_3__8_2), .in24(Reg_4__1_2),
    .in25(Reg_4__2_2), .in26(Reg_4__3_2), .in27(Reg_4__4_2), .in28(Reg_4__5_2), .in29(Reg_4__6_2),
    .in30(Reg_4__7_2), .in31(Reg_4__8_2), .out(RD1), .sel(A1), .en(not_2_out));
  Multiplexer #(.select(5), .width(32)) multiplexer_2 (
    .in0({32{1'b0}}), .in1(Reg_1__2_2), .in2(Reg_1__3_2), .in3(Reg_1__4_2), .in4(Reg_1__5_2),
    .in5(Reg_1__6_2), .in6(Reg_1__7_2), .in7(Reg_1__8_2), .in8(Reg_2__1_2), .in9(Reg_2__2_2),
    .in10(Reg_2__3_2), .in11(Reg_2__4_2), .in12(Reg_2__5_2), .in13(Reg_2__6_2), .in14(Reg_2__7_2),
    .in15(Reg_2__8_2), .in16(Reg_3__1_2), .in17(Reg_3__2_2), .in18(Reg_3__3_2), .in19(Reg_3__4_2),
    .in20(Reg_3__5_2), .in21(Reg_3__6_2), .in22(Reg_3__7_2), .in23(Reg_3__8_2), .in24(Reg_4__1_2),
    .in25(Reg_4__2_2), .in26(Reg_4__3_2), .in27(Reg_4__4_2), .in28(Reg_4__5_2), .in29(Reg_4__6_2),
    .in30(Reg_4__7_2), .in31(Reg_4__8_2), .out(RD2), .sel(A2), .en(not_3_out));
  Comparator #(.width(5)) comparator_2 (.a(A2), .b({5{1'b0}}), .eq(comparator_2_eq));  // open: gt, lt
  Comparator #(.width(5)) comparator_3 (.a(A1), .b({5{1'b0}}), .eq(comparator_3_eq));  // open: gt, lt
  not not_2 (not_2_out, comparator_3_eq);
  not not_3 (not_3_out, comparator_2_eq);
endmodule
