// Logisim project Single_Cycle_Top.circ as structural Verilog: 1 circuit, main circuit Top
module Top (
);

  wire CLK_out, not_1_out, RESET_out;
  wire [1:0] Control_Unit_controls_2;
  wire [2:0] alu_control_1_alu_control;
  wire [8:0] Control_Unit_controls;
  wire [31:0] adder_1_out, ALU_alu_result, Externder_extender_out, Instruction_Memory_instruction,
       multiplexer_1_out, multiplexer_2_out, PC_REG_q, ram_1_data, Register_File_rd1, Register_File_rd2;

  Button RESET (.out(RESET_out));
  Clock CLK (.out(CLK_out));
  not not_1 (not_1_out, RESET_out);
  Register #(.width(32)) PC_REG (.D(adder_1_out), .en(not_1_out), .Q(PC_REG_q), .clk(CLK_out), .clr(RESET_out));
  Adder #(.width(32)) adder_1 (.a(PC_REG_q), .b(32'h4), .out(adder_1_out), .cin(1'b0));  // open: cout
  Instruction_Memory Instruction_Memory (.Address(PC_REG_q[9:2]), .Instruction(Instruction_Memory_instruction));
  Register_File Register_File (
    .Clk(CLK_out), .A1(Instruction_Memory_instruction[19:15]), .WD3(multiplexer_2_out),
    .A3(Instruction_Memory_instruction[11:7]), .WE(Control_Unit_controls[8]),
    .A2(Instruction_Memory_instruction[24:20]), .RD1(Register_File_rd1), .RD2(Register_File_rd2));
  Extender Externder (
    .Data_in(Instruction_Memory_instruction[31:7]), .Imm_Src(Control_Unit_controls_2),
    .Extender_out(Externder_extender_out));
  ALU ALU (
    .Input_A(Register_File_rd1), .Input_B(multiplexer_1_out), .ALU_Control(alu_control_1_alu_control),
    .ALU_Result(ALU_alu_result));
  Multiplexer #(.width(32), .enable("false")) multiplexer_1 (
    .in0(Register_File_rd2), .in1(Externder_extender_out), .out(multiplexer_1_out),
    .sel(Control_Unit_controls[5]));
  Control_Unit Control_Unit (
    .Opcode(Instruction_Memory_instruction[6:0]),
    .Controls({Control_Unit_controls[8], Control_Unit_controls_2, Control_Unit_controls[5:0]}));
  RAM #(.addrWidth(24), .dataWidth(32), .bus("separate")) ram_1 (
    .addr(ALU_alu_result[23:0]), .din(Register_File_rd2), .data(ram_1_data), .str(Control_Unit_controls[4]),
    .sel(not_1_out), .clk(CLK_out), .clr(RESET_out));  // open: ld
  ALU_Control alu_control_1 (
    .ALU_op(Control_Unit_controls[1:0]), .Funct3(Instruction_Memory_instruction[14:12]),
    .Funct7(Instruction_Memory_instruction[29]), .op(Instruction_Memory_instruction[5]),
    .ALU_Control(alu_control_1_alu_control));
  Multiplexer #(.width(32), .enable("false")) multiplexer_2 (
    .in0(ALU_alu_result), .in1(ram_1_data), .out(multiplexer_2_out), .sel(Control_Unit_controls[3]));

  // Notes on the sheet:
  //   DATA Memory
endmodule
