// Logisim project internal_registers.circ as structural Verilog: 1 circuit, main circuit main
module main (
  input  clk,
  input  [31:0] _1,
  input  [31:0] _2,
  input  [31:0] _3,
  input  [31:0] _4,
  input  [31:0] _5,
  input  [31:0] _6,
  input  [31:0] _7,
  input  [31:0] _8,
  input  Enable,
  output [31:0] _1_2,
  output [31:0] _2_2,
  output [31:0] _3_2,
  output [31:0] _4_2,
  output [31:0] _5_2,
  output [31:0] _6_2,
  output [31:0] _7_2,
  output [31:0] _8_2
);

  Register #(.width(32), .trigger("falling")) register_1 (.D(_1), .en(Enable), .Q(_1_2), .clk(clk));  // open: clr
  Register #(.width(32), .trigger("falling")) register_2 (.D(_2), .en(Enable), .Q(_2_2), .clk(clk));  // open: clr
  Register #(.width(32), .trigger("falling")) register_3 (.D(_3), .en(Enable), .Q(_3_2), .clk(clk));  // open: clr
  Register #(.width(32), .trigger("falling")) register_4 (.D(_4), .en(Enable), .Q(_4_2), .clk(clk));  // open: clr
  Register #(.width(32), .trigger("falling")) register_5 (.D(_5), .en(Enable), .Q(_5_2), .clk(clk));  // open: clr
  Register #(.width(32), .trigger("falling")) register_6 (.D(_6), .en(Enable), .Q(_6_2), .clk(clk));  // open: clr
  Register #(.width(32), .trigger("falling")) register_7 (.D(_7), .en(Enable), .Q(_7_2), .clk(clk));  // open: clr
  Register #(.width(32), .trigger("falling")) register_8 (.D(_8), .en(Enable), .Q(_8_2), .clk(clk));  // open: clr
endmodule
