// Logisim project ALU Control.circ as structural Verilog: 1 circuit, main circuit main
module main (
  input  [1:0] in_1,
  output [2:0] out_2
);

  wire comparator_1_eq, comparator_2_eq, comparator_3_eq;
  wire [2:0] multiplexer_1_out, multiplexer_2_out, multiplexer_3_out, or_1_out, undriven;

  Comparator #(.width(2)) comparator_1 (.a(in_1), .b(2'b00), .eq(comparator_1_eq));  // open: gt, lt
  Comparator #(.width(2)) comparator_2 (.a(in_1), .b(2'b01), .eq(comparator_2_eq));  // open: gt, lt
  Comparator #(.width(2)) comparator_3 (.a(in_1), .b(2'b10), .eq(comparator_3_eq));  // open: gt, lt
  Multiplexer #(.width(3), .enable("false")) multiplexer_1 (
    .in0(3'b000), .in1(3'b000), .out(multiplexer_1_out), .sel(comparator_1_eq));
  Multiplexer #(.width(3), .enable("false")) multiplexer_2 (
    .in0(3'b000), .in1(3'b001), .out(multiplexer_2_out), .sel(comparator_2_eq));
  Multiplexer #(.width(3), .enable("false")) multiplexer_3 (
    .in0(3'b000), .in1(undriven), .out(multiplexer_3_out), .sel(comparator_3_eq));
  Multiplexer #(.select(3), .width(3), .enable("false")) multiplexer_4 (
    .in0(3'b000), .in1(3'b001), .in2(3'b101), .in3(3'b011), .in4(3'b010), .in5(3'b000), .in6(3'b000),
    .in7(3'b000), .out(out_2), .sel(or_1_out));
  assign or_1_out = multiplexer_1_out | multiplexer_2_out | multiplexer_3_out;  // OR_Gate or_1, 3 bits wide
endmodule
