// Logisim project ALU_Unit.circ as structural Verilog: 1 circuit, main circuit ALU
module ALU (
  input  [31:0] Input_A,
  input  [31:0] Input_B,
  input  [2:0] ALU_Control,
  output [31:0] ALU_Result
);

  wire comparator_1_lt;
  wire [31:0] adder_1_out, and_1_out, bit_extender_1_out, or_1_out, subtractor_1_out;

  Adder #(.width(32)) adder_1 (.a(Input_A), .b(Input_B), .out(adder_1_out), .cin(1'b0));  // open: cout
  Subtractor #(.width(32)) subtractor_1 (.a(Input_A), .b(Input_B), .out(subtractor_1_out), .bin(1'b0));  // open: bout
  assign or_1_out = Input_A | Input_B;  // OR_Gate or_1, 32 bits wide
  Comparator #(.width(32)) comparator_1 (.a(Input_A), .b(Input_B), .lt(comparator_1_lt));  // open: gt, eq
  assign and_1_out = Input_A & Input_B;  // AND_Gate and_1, 32 bits wide
  assign bit_extender_1_out = {{31{1'b0}}, comparator_1_lt};  // Bit_Extender bit_extender_1
  Multiplexer #(.select(3), .width(32)) multiplexer_1 (
    .in0(adder_1_out), .in1(subtractor_1_out), .in2(and_1_out), .in3(or_1_out), .in5(bit_extender_1_out),
    .out(ALU_Result), .sel(ALU_Control), .en(1'b1));  // open: in4, in6, in7
endmodule
