// Logisim project Basic Logic Gates and Circuits.circ as structural Verilog: 1 circuit, main circuit main
module main (
  input  in_1,
  input  in_2,
  input  in_3,
  input  in_4,
  input  in_5,
  input  XOR__GATE,
  input  in_7,
  input  in_8,
  input  in_9,
  input  in_10
);

  wire G1_out, G2_out, G3_2_out, G3_out, G4_out, not_1_out;

  and G1 (G1_out, in_1, in_2);
  or G2 (G2_out, in_3, in_4);
  not not_1 (not_1_out, in_5);
  xor G3 (G3_out, XOR__GATE, in_7);
  xor G3_2 (G3_2_out, in_8, in_9);
  LED led_1 (.in(G1_out));
  LED led_2 (.in(G2_out));
  LED led_3 (.in(not_1_out));
  LED led_4 (.in(G3_out));
  xor G4 (G4_out, G3_2_out, in_10);
  LED led_5 (.in(G4_out));

  // Notes on the sheet:
  //   AND GATE
  //   OR GATE
  //   NOT  GATE
  //   Three Way Light Control Circuit
endmodule
