// Logisim project Combinational Circuits.circ as structural Verilog: 1 circuit, main circuit main
module main (
  input  in_1,
  input  in_2,
  input  in_3,
  input  in_4,
  input  [1:0] in_5,
  input  [1:0] in_6,
  input  A,
  input  A_2,
  input  B,
  input  B_2,
  input  Cin,
  output out_12,
  output out_13,
  output out_14,
  output out_15,
  output out_16,
  output S,
  output S_2,
  output C,
  output Cout
);

  wire and_2_out, and_3_out, xor_2_out;

  Multiplexer #(.select(2), .enable("false")) multiplexer_1 (
    .in0(in_1), .in1(in_2), .in2(in_3), .in3(in_4), .out(out_15), .sel(in_6));
  xor xor_1 (S, A, B);
  and and_1 (C, A, B);
  Decoder #(.select(2), .enable("false")) decoder_1 (
    .out0(out_12), .out1(out_13), .out2(out_14), .out3(out_16), .sel(in_5));
  xor xor_2 (xor_2_out, A_2, B_2);
  and and_2 (and_2_out, A_2, B_2);
  and and_3 (and_3_out, Cin, xor_2_out);
  xor xor_3 (S_2, xor_2_out, Cin);
  or or_1 (Cout, and_2_out, and_3_out);

  // Notes on the sheet:
  //   Half Adder
  //   4x1 Mux
  //   2 by 4 Decoder
  //   Full Adder
endmodule
