// Logisim project Instrcution_memory.circ as structural Verilog: 1 circuit, main circuit Instruction_Memory
module Instruction_Memory (
  input  [7:0] Address,
  output [31:0] Instruction
);

  ROM #(.dataWidth(32)) rom_1 (.addr(Address), .data(Instruction), .sel(1'b1));

  // Notes on the sheet:
  //   contents of rom_1 (hex, n*v repeats v):
  //   ffc4a303 64a423 62e233
endmodule
