// Logisim project Main Control Unit.circ as structural Verilog: 1 circuit, main circuit main
module main (
  input  [6:0] in_1,
  output [8:0] out_2
);

  wire comparator_1_eq, comparator_2_eq, comparator_3_eq, comparator_4_eq;
  wire [2:0] multiplexer_1_out, multiplexer_2_out, multiplexer_3_out, multiplexer_4_out, or_1_out;

  Comparator #(.width(7)) comparator_1 (.a(in_1), .b(7'b0000011), .eq(comparator_1_eq));  // open: gt, lt
  Comparator #(.width(7)) comparator_2 (.a(in_1), .b(7'b0100011), .eq(comparator_2_eq));  // open: gt, lt
  Comparator #(.width(7)) comparator_3 (.a(in_1), .b(7'b0110011), .eq(comparator_3_eq));  // open: gt, lt
  Comparator #(.width(7)) comparator_4 (.a(in_1), .b(7'b1100011), .eq(comparator_4_eq));  // open: gt, lt
  Multiplexer #(.width(3), .enable("false")) multiplexer_1 (
    .in0(3'b000), .in1(3'b001), .out(multiplexer_1_out), .sel(comparator_1_eq));
  Multiplexer #(.width(3), .enable("false")) multiplexer_2 (
    .in0(3'b000), .in1(3'b010), .out(multiplexer_2_out), .sel(comparator_2_eq));
  Multiplexer #(.width(3), .enable("false")) multiplexer_3 (
    .in0(3'b000), .in1(3'b011), .out(multiplexer_3_out), .sel(comparator_3_eq));
  Multiplexer #(.width(3), .enable("false")) multiplexer_4 (
    .in0(3'b000), .in1(3'b100), .out(multiplexer_4_out), .sel(comparator_4_eq));
  assign or_1_out = multiplexer_1_out | multiplexer_2_out | multiplexer_3_out | multiplexer_4_out;  // OR_Gate or_1, 3 bits wide
  Multiplexer #(.select(3), .width(9), .enable("false")) multiplexer_5 (
    .in0({9{1'b0}}), .in1(9'h128), .in2(9'h70), .in3(9'h102), .in4(9'h85), .in5({9{1'b0}}), .in6({9{1'b0}}),
    .in7({9{1'b0}}), .out(out_2), .sel(or_1_out));
endmodule
