// Logisim project Memory Components.circ as structural Verilog: 1 circuit, main circuit main
module main (
  input  [7:0] in_1,
  input  in_2,
  input  [7:0] in_3,
  input  [3:0] in_4,
  input  in_5,
  output [7:0] out_6,
  output [7:0] out_7,
  output [3:0] out_8,
  output [3:0] out_9,
  output [3:0] out_10
);

  RAM ram_1 (.addr(in_1), .data(out_6), .ld(in_2));  // open: sel, clk, clr
  ROM rom_1 (.addr(in_3), .data(out_7));  // open: sel
  RAM #(.addrWidth(4), .dataWidth(4)) ram_2 (.addr(in_4), .data(out_8));  // open: sel, clk, ld, clr
  ROM #(.addrWidth(4), .dataWidth(4)) rom_2 (.addr(in_4), .data(out_10));  // open: sel
  Multiplexer #(.width(4), .enable("false")) multiplexer_1 (.in0(out_8), .in1(out_10), .out(out_9), .sel(in_5));

  // Notes on the sheet:
  //   Random Access Memory
  //   Read OnlyMemory
  //   Memory Based System
  //   contents of rom_1 (hex, n*v repeats v):
  //   1 2 3 4 5 6 7 8
  //   contents of rom_2 (hex, n*v repeats v):
  //   0 5 8
endmodule
