// Logisim project Sequential Circuits.circ as structural Verilog: 1 circuit, main circuit main
module main (
  input  in_1,
  input  in_2,
  input  in_3,
  input  D0,
  input  D1,
  input  D2,
  input  D3,
  output out_8,
  output out_9,
  output out_10,
  output out_11,
  output out_12,
  output out_13,
  output out_14,
  output out_15,
  output Q0,
  output Q1,
  output Q2,
  output Q3
);

  wire clock_1_out, clock_2_out, clock_3_out, clock_4_out, d_ff_2_qn, d_ff_4_qn, d_ff_7_qn, d_ff_9_qn;

  Clock clock_1 (.out(clock_1_out));
  Clock clock_2 (.out(clock_2_out));
  Clock clock_3 (.out(clock_3_out));
  D_Flip_Flop d_ff_1 (.clk(clock_1_out), .D(D0), .Q(out_12));  // open: Qn, preset, en, reset
  D_Flip_Flop d_ff_2 (.clk(clock_2_out), .D(d_ff_2_qn), .Q(Q0), .Qn(d_ff_2_qn));  // open: preset, en, reset
  S_R_Flip_Flop s_r_ff_1 (.S(in_1), .clk(clock_3_out), .R(in_3), .Q(out_8), .Qn(out_10));  // open: preset, reset, en
  D_Flip_Flop d_ff_3 (.clk(clock_1_out), .D(D1), .Q(out_13));  // open: Qn, preset, en, reset
  D_Flip_Flop d_ff_4 (.clk(d_ff_2_qn), .D(d_ff_4_qn), .Q(Q1), .Qn(d_ff_4_qn));  // open: preset, en, reset
  Clock clock_4 (.out(clock_4_out));
  D_Flip_Flop d_ff_5 (.clk(clock_4_out), .D(in_2), .Q(out_9), .Qn(out_11));  // open: preset, en, reset
  D_Flip_Flop d_ff_6 (.clk(clock_1_out), .D(D2), .Q(out_14));  // open: Qn, preset, en, reset
  D_Flip_Flop d_ff_7 (.clk(d_ff_4_qn), .D(d_ff_7_qn), .Q(Q2), .Qn(d_ff_7_qn));  // open: preset, en, reset
  D_Flip_Flop d_ff_8 (.clk(clock_1_out), .D(D3), .Q(out_15));  // open: Qn, preset, en, reset
  D_Flip_Flop d_ff_9 (.clk(d_ff_7_qn), .D(d_ff_9_qn), .Q(Q3), .Qn(d_ff_9_qn));  // open: preset, en, reset

  // Notes on the sheet:
  //   SR Flip Flop
  //   4 Bit Register
  //   4 Bit Asynchronous Counter
  //   D Flip Flop
endmodule
